# Fritzing sketch OttawaBadgeAnimationRemote (saved by Fritzing 0.9.2b)
breadboards: 2

parts:
  USB-Boarduino_v2_1 = Boarduino
  KEYPAD1 = Membrane Matrix Keypad
  R1 = Resistor [tolerance=±5% resistance=100 package=THT]
  LED1 = smd LED [color="Infrared (940nm)" package="0603 [SMD]"]  # not connected

nets:
  N1: USB-Boarduino_v2_1.d3, R1.Pin_0
  N2: USB-Boarduino_v2_1.d10, KEYPAD1.7
  N3: USB-Boarduino_v2_1.d11, KEYPAD1.6
  N4: USB-Boarduino_v2_1.d12, KEYPAD1.5
  N5: USB-Boarduino_v2_1.a0, KEYPAD1.4
  N6: USB-Boarduino_v2_1.a1, KEYPAD1.3
  N7: USB-Boarduino_v2_1.a2, KEYPAD1.2
  N8: USB-Boarduino_v2_1.a3, KEYPAD1.1

custom parts:
  Membrane Matrix Keypad: Membrane Matrix 3x4 Keypad
