# Fritzing sketch OttawaBadgeBaseStation (saved by Fritzing 0.9.2b)
circuit board: 8.46667cm x 5.64444cm
breadboards: 1

parts:
  LED1 = LED - 5mm [color="Infrared (940nm)" package="5 mm [THT]"]
  R1 = Resistor [tolerance=±5% resistance=100 package=THT]
  IR1 = TSOP312.., 314.. [package=THT]
  C1 = Ceramic Capacitor [capacitance="100 nF" package="200 mil [THT, multilayer]"]
  Part1 = Arduino Uno (Rev3)

nets:
  N1: LED1.cathode, R1.Pin_1
  N2: LED1.anode, Part1.D3_PWM
  GND: R1.Pin_0, IR1.GND, C1.0, Part1.GND
  N3: IR1.Vs, C1.1, Part1.5V
  N4: IR1.Data, Part1.D9_PWM
